# Fritzing sketch 499_wt (saved by Fritzing 1.0.6)
breadboards: 1

parts:
  Part1 = Arduino Uno (Rev3)
  Part2 = DeadOn RTC - DS3234 Breakout
  Part3 = OpenLog
  LED4 = LED - 5mm [color="Red (633nm)" current=0.030A package="5 mm [THT]"]
  LED5 = LED - 5mm [color="Red (633nm)" current=0.030A package="5 mm [THT]"]
  LED6 = LED - 5mm [color="Red (633nm)" current=0.030A package="5 mm [THT]"]
  LED7 = LED - 5mm [color="Infrared (940nm)" current=0.030A package="5 mm [THT]"]
  LED8 = LED - 5mm [color="Infrared (940nm)" current=0.030A package="5 mm [THT]"]
  LED9 = LED - 5mm [color="Infrared (940nm)" current=0.030A package="5 mm [THT]"]
  U1 = DCM01 Reflective Blood Sensor [package=dcm01]

nets:
  N1: Part1.A0, U1.2
  N2: Part1.A1, U1.3
  N3: Part1.D8, LED6.cathode
  N4: Part1.D10_PWM/SS, Part2.SS
  N5: Part1.D11_PWM/MOSI, Part2.MOSI
  N6: Part1.D12/MISO, Part2.MISO
  N7: Part1.D13/SCK, Part2.SCLK
  N8: Part1.D1/TX, Part3.RXI
  N9: Part1.D2, Part2.INT/SQW
  N10: Part1.D3_PWM, LED7.cathode
  N11: Part1.D4, LED8.cathode
  N12: Part1.D5_PWM, LED9.cathode
  N13: Part1.D6_PWM, LED4.cathode
  N14: Part1.D7, LED5.cathode
  VCC: Part1.5V, Part2.VCC, Part3.VCC, U1.1
  GND: Part1.GND, Part2.GND, Part3.GND, LED4.anode, LED5.anode, LED6.anode, LED7.anode, LED8.anode, LED9.anode, U1.4
